# Fritzing sketch A08Fritzing (saved by Fritzing 0.9.3b)
breadboards: 1

parts:
  LED1 = LED - 5mm [color="Yellow (595nm)" package="5 mm [THT]"]
  LED2 = LED - 5mm [color="Green (570nm)" package="5 mm [THT]"]
  LED3 = LED - 5mm [color="Blue (470nm)" package="5 mm [THT]"]
  LED4 = LED - 5mm [color="White (4500K)" package="5 mm [THT]"]
  LED5 = LED - 5mm [color="Red (633nm)" package="5 mm [THT]"]
  R1 = Resistor [tolerance=±5% resistance=220 package=THT]
  R2 = Resistor [tolerance=±5% resistance=330 package=THT]
  R3 = Resistor [tolerance=±5% resistance=15 package=THT]
  R4 = Resistor [tolerance=±5% resistance=15 package=THT]
  R5 = Resistor [tolerance=±5% resistance=75 package=THT]
  J1 = STM32 Nucleo boards
  J2 = Basic Servo
  Componente1 = Breakout Board for Electret Microphone

nets:
  N1: LED1.cathode, LED2.cathode, LED3.cathode, LED4.cathode, LED5.cathode, J1.GND
  N2: LED1.anode, R2.Pin_1
  N3: LED2.anode, R1.Pin_1
  N4: LED3.anode, R3.Pin_1
  N5: LED4.anode, R4.Pin_1
  N6: LED5.anode, R5.Pin_1
  N7: R1.Pin_0, J1.D13/SCK
  N8: R2.Pin_0, J1.D12/MISO
  N9: R3.Pin_0, J1.D10_PWM/SS
  N10: R4.Pin_0, J1.D9_PWM
  N11: R5.Pin_0, J1.D11_PWM/MOSI
  N12: J1.A0, J2.vcc, J2.pulse
  N13: J1.A1, Componente1.AUD
