# Fritzing sketch Lab1 (saved by Fritzing 0.9.3b)
breadboards: 1

parts:
  LED1 = LED - 5mm [color="Yellow (585nm)" package="5 mm [THT]"]
  LED2 = LED - 5mm [color="Red (633nm)" package="5 mm [THT]"]
  J1 = STM32 Nucleo boards
  R1 = Resistor [tolerance=±5% resistance=330 package=THT]
  R2 = Resistor [tolerance=±5% resistance=75 package=THT]
  Grove2 = Grove Button

nets:
  N1: LED1.cathode, LED2.cathode, J1.GND
  N2: LED1.anode, R1.Pin_0
  N3: LED2.anode, R2.Pin_0
  N4: J1.D13/SCK, R2.Pin_1
  N5: J1.D2, Grove2.SIG
  N6: J1.D6_PWM, R1.Pin_1
