# Fritzing sketch lab1Fritzing (saved by Fritzing 0.9.3b)
breadboards: 1

parts:
  J1 = STM32 Nucleo boards
  R1 = Resistor [tolerance=±5% resistance=330 package=THT]
  S1 = Momentary Switch [package=ksa_sealed_tac_switch]
  LED1 = smd LED [color="Red (633nm)" package="1206 [SMD]"]
  LED2 = smd LED [color="Yellow (595nm)" package="1206 [SMD]"]
  R2 = Resistor [tolerance=±5% resistance=75 package=THT]
  R3 = Resistor [tolerance=±5% resistance=220 package=THT]
  R4 = Resistor [tolerance=±5% resistance=220 package=THT]  # not connected

nets:
  N1: J1.D13/SCK, R2.Pin_0
  N2: J1.D2, S1.4
  N3: J1.D6_PWM, R3.Pin_0
  N4: J1.3V3, S1.1
  N5: J1.GND, R1.Pin_0, LED1.cathode, LED2.cathode
  N6: R1.Pin_1, S1.3
  N7: LED1.anode, R2.Pin_1
  N8: LED2.anode, R3.Pin_1
